# Fritzing sketch Módulo_GSM (saved by Fritzing 0.9.9b)

parts:
  Componente3 = Arduino Uno (Rev3)
  SIM800L_BO4 = SIM800L BO
  Bat3 = battery_holder_single_18650
  Bat4 = battery_holder_single_18650
  U4 = LM2596 step down module

nets:
  N1: Componente3.GND, SIM800L_BO4.pin_6, Bat4.+#0, U4.IN-, U4.OUT-
  N2: Componente3.D2, SIM800L_BO4.pin_4
  N3: Componente3.D3_PWM, SIM800L_BO4.pin_5
  N4: SIM800L_BO4.PIN2, U4.OUT+
  N5: Bat3.+#0, Bat4.+#1
  N6: Bat3.+#1, U4.IN+

notes:
  PINOS GSM x ARDUINO
  GSM Arduino UNO
  TX D2
  RX D3
  GND GND
  VCC Steep Donw

custom parts:
  battery_holder_single_18650: single 18650 battery holder
  LM2596 step down module: LM2596 DC-DC step down power supply module 3 A.
